# Fritzing sketch XIAO SOCD Cleaner (saved by Fritzing 0.9.5d)
breadboards: 1

parts:
  R1 = Resistor [tolerance=±5% resistance=100 package=THT]
  PC847 = IC, DIP package, 16 pins [chip_label=PC847]
  R2 = Resistor [tolerance=±5% resistance=100 package=THT]
  R3 = Resistor [tolerance=±5% resistance=100 package=THT]
  R4 = Resistor [tolerance=±5% resistance=100 package=THT]
  Output = female alternating pin header, 5 pins [form="♀ (female)"]
  Input = female alternating pin header, 5 pins [form="♀ (female)"]
  POWER = female pin header, 2 pins [form="♀ (female)"]
  SW1 = DIP SWITCH [package=dipswitch-02]
  Mod1 = seeeduino-xiao

nets:
  N1: R1.Pin_0, PC847.pin7
  N2: R1.Pin_1, Mod1.D4
  N3: PC847.pin1, R2.Pin_0
  N4: PC847.pin2, PC847.pin4, PC847.pin6, PC847.pin8, POWER.pin1
  N5: PC847.pin3, R3.Pin_0
  N6: PC847.pin5, R4.Pin_0
  N7: PC847.pin9, PC847.pin11, PC847.pin13, PC847.pin15, Output.pin5
  N8: PC847.pin10, Output.pin4
  N9: PC847.pin12, Output.pin3
  N10: PC847.pin14, Output.pin2
  N11: PC847.pin16, Output.pin1
  N12: R2.Pin_1, Mod1.D10
  N13: R3.Pin_1, Mod1.D9
  N14: R4.Pin_1, Mod1.D8
  N15: Input.pin1, Mod1.D3
  N16: Input.pin2, Mod1.D2
  N17: Input.pin3, Mod1.D1
  N18: Input.pin4, Mod1.D0
  N19: Input.pin5, SW1.1, SW1.2, Mod1.GND
  N20: POWER.pin2, Mod1.3V3
  N21: SW1.3, Mod1.D5
  N22: SW1.4, Mod1.D6

custom parts:
  seeeduino-xiao: Seeeduino XIAO processor board.
